# Fritzing sketch sequencino (saved by Fritzing 0.9.1b)
breadboards: 3

parts:
  S2 = Pushbutton [package="[THT]"]
  S2_2 = Pushbutton [package="[THT]"]
  R3 = Resistor [resistance=1k tolerance=±5% package=THT]
  R3_2 = Resistor [resistance=1k tolerance=±5% package=THT]
  R3_3 = Resistor [resistance=1k tolerance=±5% package=THT]
  R3_4 = Resistor [resistance=1k tolerance=±5% package=THT]
  R3_5 = Resistor [resistance=1k tolerance=±5% package=THT]
  R3_6 = Resistor [resistance=1k tolerance=±5% package=THT]
  R3_7 = Resistor [resistance=1k tolerance=±5% package=THT]
  R3_8 = Resistor [resistance=1k tolerance=±5% package=THT]
  R3_9 = Resistor [resistance=1k tolerance=±5% package=THT]
  R3_10 = Resistor [resistance=1k tolerance=±5% package=THT]
  DIN1 = DIN-5 jack (MIDI) [package=THT]
  R4 = Resistor [resistance=220 tolerance=±5% package=THT]
  R5 = Resistor [resistance=10k tolerance=±5% package=THT]
  R5_2 = Resistor [resistance=10k tolerance=±5% package=THT]
  LED3 = LED - 5mm [color="Yellow (585nm)" package="5 mm [THT]"]
  LED5 = LED - 5mm [color="Yellow (585nm)" package="5 mm [THT]"]
  LED8 = LED - 5mm [color="Yellow (585nm)" package="5 mm [THT]"]
  LED1 = LED - 5mm [color="Yellow (585nm)" package="5 mm [THT]"]
  LED6 = LED - 5mm [color="Yellow (585nm)" package="5 mm [THT]"]
  LED10 = LED - 5mm [color="Red (633nm)" package="5 mm [THT]"]
  LED4 = LED - 5mm [color="Yellow (585nm)" package="5 mm [THT]"]
  R2 = Rotary Potentiometer (Small) [maximum_resistance=100kΩ package=THT]  # not connected
  LED2 = LED - 5mm [color="Yellow (585nm)" package="5 mm [THT]"]
  LED7 = LED - 5mm [color="Yellow (585nm)" package="5 mm [THT]"]
  LED9 = LED - 5mm [color="Green (555nm)" package="5 mm [THT]"]
  DIN2 = DIN-5 jack (MIDI) [package=THT]
  IC1 = IC, DIP package, 8 pins [chip_label=IC]
  R6 = Resistor [tolerance=±5% resistance=220 package=THT]
  D1 = Rectifier Diode [part_number=1N4001 package="300 mil [THT]"]
  R7 = Resistor [tolerance=±5% resistance=10k package=THT]
  R8 = Resistor [tolerance=±5% resistance=470 package=THT]
  U1 = atmega328 [package=dip]
  R9 = Resistor [tolerance=±5% resistance=10k package=THT]
  C1 = Ceramic Capacitor [capacitance=10pF package="100 mil [THT, multilayer]"]
  C2 = Ceramic Capacitor [capacitance=10pF package="100 mil [THT, multilayer]"]
  XTAL1 = Crystal [frequency="16 Mhz" package=THT]
  J1 = Power Jack [package=power_jack_pth_lock]

nets:
  N1: S2.Pin_1, S2.Pin_2, S2_2.Pin_1, S2_2.Pin_2, U1.VCC, U1.AVCC, U1.AREF, R9.Pin_1, J1.GNDBREAK
  N2: S2.Pin_3, S2.Pin_4, R5_2.Pin_0, U1.A0
  N3: S2_2.Pin_3, S2_2.Pin_4, R5.Pin_0, U1.A1
  N4: R3.Pin_0, LED10.cathode
  N5: R3.Pin_1, R3_2.Pin_1, R3_3.Pin_1, R3_4.Pin_1, R3_5.Pin_1, R3_6.Pin_1, R3_7.Pin_1, R3_8.Pin_1, R3_9.Pin_1, R3_10.Pin_1, R5.Pin_1, R5_2.Pin_1, U1.GND, C1.0, C2.1, J1.PWR
  N6: R3_2.Pin_0, LED9.cathode
  N7: R3_3.Pin_0, LED8.cathode
  N8: R3_4.Pin_0, LED7.cathode
  N9: R3_5.Pin_0, LED6.cathode
  N10: R3_6.Pin_0, LED5.cathode
  N11: R3_7.Pin_0, LED4.cathode
  N12: R3_8.Pin_0, LED3.cathode
  N13: R3_9.Pin_0, LED2.cathode
  N14: R3_10.Pin_0, LED1.cathode
  N15: DIN1.5, U1.D1_(TX)
  N16: DIN1.2, IC1.pin5, R7.Pin_1
  N17: DIN1.4, R4.Pin_0
  N18: R4.Pin_1, IC1.pin8, R8.Pin_0
  N19: LED3.anode, U1.D11_(PWM)
  N20: LED5.anode, U1.D9_(PWM)
  N21: LED8.anode, U1.D6_(PWM)
  N22: LED1.anode, U1.D13
  N23: LED6.anode, U1.D8
  N24: LED10.anode, U1.D4
  N25: LED4.anode, U1.D10_(PWM)
  N26: LED2.anode, U1.D12
  N27: LED7.anode, U1.D7
  N28: LED9.anode, U1.D5_(PWM)
  N29: DIN2.5, R6.Pin_0
  N30: DIN2.4, IC1.pin2, D1.cathode
  N31: IC1.pin3, R6.Pin_1, D1.anode
  N32: IC1.pin6, R8.Pin_1, U1.D0_(RX)
  N33: IC1.pin7, R7.Pin_0
  N34: U1.RESET, R9.Pin_0
  N35: U1.XLAT1, C2.0, XTAL1.pin_1
  N36: U1.XLAT2, C1.1, XTAL1.pin_0
